# Fritzing sketch connections (saved by Fritzing 0.8.5b)
circuit board: 8.46667cm x 5.64444cm

parts:
  Part2 = Arduino Due (Rev2b)
  U1 = SPI_FLASH-X25XX [package=so08]
  U1_2 = AT45DB041B [package=so08wide]
  U1_3 = AT25FS010 [package=so08wide]

nets:
  GND: Part2.GND, U1.GND, U1_2.GND, U1_3.GND
  N1: U1.CS, U1_2.CS, U1_3.CS
  VCC: U1.WP, U1.VCC, U1_2.WP, U1_2.VCC, U1_3.WP, U1_3.VCC
  N2: U1.SCK, U1_2.SCK, U1_3.SCK

notes:
  /CS
  DO
  /WP
  GND
  VCC
  CLK
  /HOLD
  DI
